# Fritzing sketch diagram (saved by Fritzing 0.9.10b)
breadboards: 2

parts:
  Part7 = NRF24L01+ Breakout Board
  LED7 = LED - 5mm [color="Yellow (595nm)" current=0.030 package="5 mm [THT]"]
  Part6 = Arduino Nano (Rev3.0) [part_number=1]
  C1 = Electrolytic Capacitor [capacitance=10µF voltage=16V package="0807 [SMD, electrolytic]"]
  SP3 = SPEAKER [package=pcb_mount_speaker]
  Part5 = NRF24L01+ Breakout Board
  VCC2 = 4 x AAA Battery Mount
  R16 = Resistor [tolerance=±5% power=0.25 resistance=220 package=THT]
  SP2 = SPEAKER [package=pcb_mount_speaker]
  LED9 = LED - 5mm [color="Red (633nm)" current=0.030 package="5 mm [THT]"]
  VCC3 = 4 x AAA Battery Mount
  Part8 = Arduino Nano (Rev3.0) [part_number=1]
  LED5 = LED - 5mm [color="Green (560nm)" current=0.030 package="5 mm [THT]"]
  Part1 = MQ-3 breakout
  C2 = Electrolytic Capacitor [capacitance=10µF voltage=16V package="0807 [SMD, electrolytic]"]
  R14 = Resistor [tolerance=±5% power=0.25 resistance=220 package=THT]
  R17 = Resistor [tolerance=±5% power=0.25 resistance=220 package=THT]
  LED8 = LED - 5mm [color="Yellow (595nm)" current=0.030 package="5 mm [THT]"]
  R7 = Resistor [tolerance=±5% power=0.25 resistance=220 package=THT]
  R11 = Resistor [tolerance=±5% power=0.25 resistance=220 package=THT]
  LED10 = LED - 5mm [color="Green (560nm)" current=0.030 package="5 mm [THT]"]
  R10 = Resistor [tolerance=±5% power=0.25 resistance=220 package=THT]
  LED6 = LED - 5mm [color="Red (633nm)" current=0.030 package="5 mm [THT]"]

nets:
  GND: Part7.GND, C1.-, SP3.+, LED9.cathode, VCC3.-, Part8.GND, Part1.GND, LED8.cathode, LED10.cathode
  VCC: Part7.VCC, C1.+, Part8.3V3
  N1: Part7.CE, Part8.D7
  N2: Part7.CS, Part8.D8
  N3: Part7.SCK, Part8.D13/SCK
  N4: Part7.MOSI, Part8.D11/MOSI
  N5: Part7.MISO, Part8.D12/MISO
  N6: LED7.cathode, SP2.+, LED5.cathode, LED6.cathode
  N7: LED7.anode, Part6.D3, R10.Pin_0, R10.Pin_1
  GND_2: Part6.GND, Part5.GND, VCC2.-, C2.-
  N8: Part6.D2, LED5.anode, R11.Pin_0, R11.Pin_1
  N9: Part6.D4, R7.Pin_0, R7.Pin_1, LED6.anode
  N10: Part6.D5, SP2.-
  N11: Part6.D7, Part5.CE
  N12: Part6.D8, Part5.CS
  N13: Part6.D11/MOSI, Part5.MOSI
  N14: Part6.D12/MISO, Part5.MISO
  N15: Part6.VIN, VCC2.+
  3V3: Part6.3V3, Part5.VCC, C2.+
  N16: Part6.D13/SCK, Part5.SCK
  N17: SP3.-, Part8.D5
  N18: R16.Pin_0, R16.Pin_1, Part8.D2, LED10.anode
  N19: LED9.anode, Part8.D4, R17.Pin_0, R17.Pin_1
  N20: VCC3.+, Part8.VIN
  N21: Part8.D3, R14.Pin_0, R14.Pin_1, LED8.anode
  5V: Part8.5V, Part1.VCC
  N22: Part8.A7, Part1.AO

notes:
  Sensor unit
  Central unit

custom parts:
  MQ-3 breakout: Alcohol sensor is capable of detecting alcohol (ethanol) particles on itself and gives the information in digital form back to us to manipulate with it. SKU:101251 • Voltage: 5V DC • Power: max 750mW • Measurement range: 0.04-4mg/L
